# Fritzing sketch hcsr04_distance (saved by Fritzing 0.9.10b)
breadboards: 1

parts:
  Part1 = Adafruit Feather M4 Express [part_number="Adafruit #3857"]
  Part2 = SRF05 Ultrasonic Rangefinder
  R2 = Resistor [tolerance=±5% resistance=10k package="0805 [SMD]"]
  R1 = Resistor [tolerance=±5% resistance=10k package="0805 [SMD]"]

nets:
  N1: Part1.A5, R2.Pin_0, R1.Pin_1
  N2: Part1.A4, Part2.Trig
  GND: Part1.GND, Part2.GND, R2.Pin_1
  N3: Part1.VBUS, Part2.VCC
  N4: Part2.Echo, R1.Pin_0

custom parts:
  Adafruit Feather M4 Express: It's what you've been waiting for, the Feather M4 Express featuring ATSAMD51. This Feather is fast like a swift, smart like an owl, strong like a ox-bird (it's half ox, half bird, OK?) This feather is powered by our new favorite chip, the ATSAMD51J19 - with its 120MHz Cortex M4 with floating point support and 512KB Flash and 192KB RAM. Your code will zig and zag and zoom, and with a bunch of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
